# Fritzing sketch Perfboard (saved by Fritzing 0.9.5d)
circuit board: 6.5cm x 6.5cm
perfboards: 1

parts:
  J1 = female pin header, 10 pins [form="♀ (female)"]
  J2 = female pin header, 10 pins [form="♀ (female)"]
  Q1 = Basic FET N-Channel [package="TO220 [THT]"]
  R1 = Rotary Potentiometer (Large) [maximum_resistance=10kΩ package=THT]
  U1 = Voltage Regulator - 5V [package="TO220 [THT]"]
  J4 = male pin header, 2 pins [form="♂ (male)"]
  J5 = double row male pin header, 2 pins [form="♂ (male)"]
  J6 = male pin header, 5 pins [form="♂ (male)"]
  R2 = Resistor [tolerance=±5% resistance=22k package=THT]
  R3 = Resistor [tolerance=±5% resistance=1k package=THT]
  J7 = Piezo Speaker
  U2 = LCD-16X2 [package=lcd-16x2]

nets:
  LCD_RS: J1.pin1, U2.RS
  POT: J1.pin2, R1.wiper
  GATE: J1.pin5, Q1.gate
  BUZZ: J1.pin6, J7.pin1
  GND: J1.pin7, Q1.source, R1.leg1, U1.GND, J4.pin2, J6.pin5, R3.Pin_1, J7.pin2, U2.VSS, U2.K
  5V: J1.pin8, J1.pin9, R1.leg2, U1.output_voltage, J6.pin4, R2.Pin_0, U2.VDD, U2.A
  MAX_CS: J1.pin10, J6.pin2
  LCD_RW: J2.pin1, U2.R_W
  LCD_EN: J2.pin2, U2.E
  MAX_SO: J2.pin4, J6.pin1
  MAX_SCK: J2.pin6, J6.pin3
  LCD_D4: J2.pin7, U2.DB4
  LCD_D5: J2.pin8, U2.DB5
  LCD_D6: J2.pin9, U2.DB6
  LCD_D7: J2.pin10, U2.DB7
  N1: Q1.drain, J5.pin2
  24V: U1.input_voltage, J4.pin1, J5.pin1
  LCD_VO: R2.Pin_1, R3.Pin_0, U2.VO
